# Fritzing sketch ArduinoSerialServer (saved by Fritzing 0.9.3b)
breadboards: 2

parts:
  R1 = Resistor [tolerance=±5% resistance=330 package="2010 [SMD]"]  # not connected
  LED1 = LED - 3mm [color="Red (633nm)" package="3 mm [THT]"]
  Composant1 = Arduino Micro (Rev3)  # not connected
  LED2 = LED - 3mm [color="Red (633nm)" package="3 mm [THT]"]
  LED3 = LED - 3mm [color="Red (633nm)" package="3 mm [THT]"]
  LED4 = LED - 3mm [color="Red (633nm)" package="3 mm [THT]"]
  R2 = Resistor [tolerance=±5% resistance=330 package="2010 [SMD]"]
  R3 = Resistor [tolerance=±5% resistance=330 package="2010 [SMD]"]  # not connected
  R4 = Resistor [tolerance=±5% resistance=330 package="2010 [SMD]"]  # not connected
  R5 = Resistor [tolerance=±5% resistance=330 package="2010 [SMD]"]
  LED5 = LED - 3mm [color="Red (633nm)" package="3 mm [THT]"]
  LED6 = LED - 3mm [color="Red (633nm)" package="3 mm [THT]"]
  LED7 = LED - 3mm [color="Red (633nm)" package="3 mm [THT]"]
  LED8 = LED - 3mm [color="Red (633nm)" package="3 mm [THT]"]
  R6 = Resistor [tolerance=±5% resistance=330 package="2010 [SMD]"]  # not connected
  R7 = Resistor [tolerance=±5% resistance=330 package="2010 [SMD]"]
  R8 = Resistor [tolerance=±5% resistance=330 package="2010 [SMD]"]

nets:
  N1: LED1.cathode, LED2.cathode, LED3.cathode, LED4.cathode, R2.Pin_0, R2.Pin_1, LED5.cathode, LED6.cathode, LED7.cathode, LED8.cathode
  N2: R5.Pin_1, LED8.anode
  N3: LED5.anode, R7.Pin_1
  N4: LED7.anode, R8.Pin_1
